// Logisim project rp.circ as structural Verilog: 1 circuit, main circuit main
module main (
  input  [7:0] in_1,
  input  in_2
);

  wire adder_1_cout, and_1_out, and_2_out, and_3_out, and_4_out, and_5_out, and_6_out, and_7_out, M_FLAG_C_q,
       M_FLAG_E_q, M_FLAG_M_q, m_flag_set_carry, m_flag_set_emu, m_flag_set_mem, m_flag_set_zero, M_FLAG_Z_q,
       m_load_opcode, m_load_uop_low, m_mux_in_flag_emu, m_PC_to_PC, m_reset_clear, m_VEC_RESET_to_PC,
       multiplexer_3_out, multiplexer_4_out, multiplexer_6_out, multiplexer_8_out, multiplexer_9_out,
       not_1_out, not_2_out, not_3_out, not_4_out, not_5_out, not_6_out, not_8_out, not_9_out, not_10_out,
       not_11_out, not_12_out, not_13_out, or_1_out, PIN_CLK, PIN_R_nW, PIN_RESET, re_reset_sig,
       RESET_ASYNC_q, S_FLAG_C, S_FLAG_E, S_FLAG_M, S_FLAG_Z, s_pc_increment, s_PC_to_ADDR, S_RESET_q,
       s_write_mode;
  wire [1:0] m_mux_in_flag_mem, m_mux_in_flag_zero;
  wire [2:0] m_mux_in_flag_carry;
  wire [7:0] adder_1_out, adder_2_out, BUS_ADDR_HIGH, BUS_ADDR_LOW, controlled_buffer_1_out,
       controlled_buffer_2_out, counter_1_q, M_DATA_q, M_OPCODE_q, M_PC_HIGH_q, M_PC_LOW_q,
       multiplexer_7_out, PIN_DATA, ram_1_data, rom_1_data, S_PC_HIGH_q, S_PC_LOW_q;
  wire [7:2] rom_5_data;
  wire [7:3] rom_3_data;
  wire [7:4] rom_7_data;
  wire [9:0] M_UPC_q, multiplexer_1_out, multiplexer_2_out, rom_2_data, rom_4_data, S_UPC_q;
  wire [15:0] multiplexer_5_out, PIN_ADDR;

  Clock clock_1 (.out(PIN_CLK));
  assign controlled_buffer_1_out = m_VEC_RESET_to_PC ? 8'h3 : 8'bz;  // Controlled_Buffer controlled_buffer_1
  Multiplexer #(.width(10), .enable("false")) multiplexer_1 (
    .in0(rom_2_data), .in1(10'h1), .out(multiplexer_1_out), .sel(re_reset_sig));
  Multiplexer #(.width(10), .enable("false")) multiplexer_2 (
    .in0(rom_4_data), .in1(multiplexer_1_out), .out(multiplexer_2_out), .sel(m_load_uop_low));
  Multiplexer #(.select(3), .disabled(0), .enable("false")) multiplexer_3 (
    .in0(1'b0), .in1(1'b1), .in2(in_1[0]), .in3(S_FLAG_E), .in4(in_2), .out(multiplexer_3_out),
    .sel(m_mux_in_flag_carry));  // open: in5, in6, in7
  Multiplexer #(.select(2), .disabled(0), .enable("false")) multiplexer_4 (.out(multiplexer_4_out));  // open: in0, in1, in2, in3, sel
  Counter #(.trigger("falling")) counter_1 (.Q(counter_1_q), .clk(and_1_out));  // open: load, D, count, carry, clr
  and and_1 (and_1_out, PIN_CLK, PIN_RESET);
  assign controlled_buffer_2_out = m_VEC_RESET_to_PC ? {8{1'b1}} : 8'bz;  // Controlled_Buffer controlled_buffer_2
  Register #(.width(1), .trigger("high")) M_FLAG_C (
    .D(multiplexer_3_out), .Q(M_FLAG_C_q), .clk(and_2_out));  // open: en, clr
  and and_2 (and_2_out, m_flag_set_carry, PIN_CLK);
  Register #(.width(1), .trigger("high")) M_FLAG_E (
    .D(multiplexer_4_out), .Q(M_FLAG_E_q), .clk(PIN_CLK));  // open: en, clr
  Comparator #(.mode("unsigned")) comparator_1 (.a(counter_1_q), .b(8'h4), .lt(PIN_RESET));  // open: gt, eq
  assign controlled_buffer_2_out = m_PC_to_PC ? S_PC_LOW_q : 8'bz;  // Controlled_Buffer controlled_buffer_3
  assign controlled_buffer_1_out = m_PC_to_PC ? S_PC_HIGH_q : 8'bz;  // Controlled_Buffer controlled_buffer_4
  or or_1 (or_1_out, PIN_RESET, m_reset_clear);
  and and_3 (and_3_out, ~PIN_RESET, m_reset_clear);  // AND_Gate
  not not_1 (not_1_out, PIN_CLK);
  Register #(.width(1), .trigger("high")) u_S_FLAG_C (.D(M_FLAG_C_q), .Q(S_FLAG_C), .clk(not_2_out));  // open: en, clr
  not not_2 (not_2_out, PIN_CLK);
  Register #(.width(1), .trigger("high")) u_S_FLAG_E (.D(M_FLAG_E_q), .Q(S_FLAG_E), .clk(not_3_out));  // open: en, clr
  not not_3 (not_3_out, PIN_CLK);
  ROM rom_1 (.addr(counter_1_q), .data(rom_1_data));  // open: sel
  Register #(.trigger("high")) M_PC_LOW (.D(controlled_buffer_2_out), .Q(M_PC_LOW_q), .clk(PIN_CLK));  // open: en, clr
  Register #(.trigger("high")) M_PC_HIGH (
    .D(controlled_buffer_1_out), .Q(M_PC_HIGH_q), .clk(PIN_CLK));  // open: en, clr
  S_R_Flip_Flop #(.trigger("high")) RESET_ASYNC (
    .S(PIN_RESET), .clk(or_1_out), .R(and_3_out), .Q(RESET_ASYNC_q));  // open: Qn, preset, reset, en
  Register #(.trigger("high")) M_DATA (.D(PIN_DATA), .Q(M_DATA_q), .clk(PIN_CLK));  // open: en, clr
  Register #(.trigger("high")) M_OPCODE (.D(M_DATA_q), .Q(M_OPCODE_q), .clk(and_4_out));  // open: en, clr
  and and_4 (and_4_out, PIN_CLK, m_load_opcode);
  Register #(.width(10), .trigger("high")) M_UPC (.D(multiplexer_2_out), .Q(M_UPC_q), .clk(PIN_CLK));  // open: en, clr
  Register #(.width(10), .trigger("high")) S_UPC (.D(M_UPC_q), .Q(S_UPC_q), .clk(not_1_out));  // open: en, clr
  Multiplexer #(.width(16), .enable("false")) multiplexer_5 (
    .in0(PIN_ADDR), .in1({8'h4, counter_1_q}), .out(multiplexer_5_out), .sel(PIN_RESET));
  Multiplexer #(.enable("false")) multiplexer_6 (.in0(PIN_R_nW), .in1(1'b0), .out(multiplexer_6_out), .sel(PIN_RESET));
  Multiplexer #(.width(8), .enable("false")) multiplexer_7 (
    .in0(PIN_DATA), .in1(rom_1_data), .out(multiplexer_7_out), .sel(PIN_RESET));
  Register #(.trigger("high")) S_ADDR_LOW (.D(BUS_ADDR_LOW), .Q(PIN_ADDR[7:0]), .clk(not_4_out));  // open: en, clr
  not not_4 (not_4_out, PIN_CLK);
  Register #(.trigger("high")) S_ADDR_HIGH (.D(BUS_ADDR_HIGH), .Q(PIN_ADDR[15:8]), .clk(not_5_out));  // open: en, clr
  not not_5 (not_5_out, PIN_CLK);
  Adder adder_1 (.a(M_PC_LOW_q), .b({8{1'b0}}), .out(adder_1_out), .cin(s_pc_increment), .cout(adder_1_cout));
  Adder adder_2 (.a(M_PC_HIGH_q), .b({8{1'b0}}), .out(adder_2_out), .cin(adder_1_cout));  // open: cout
  Register #(.width(1), .trigger("high")) S_RESET (.D(RESET_ASYNC_q), .Q(S_RESET_q), .clk(not_6_out));  // open: en, clr
  not not_6 (not_6_out, PIN_CLK);
  not not_7 (PIN_R_nW, s_write_mode);
  Register #(.trigger("high")) S_PC_LOW (.D(adder_1_out), .Q(S_PC_LOW_q), .clk(not_8_out));  // open: en, clr
  not not_8 (not_8_out, PIN_CLK);
  Register #(.trigger("high")) S_PC_HIGH (.D(adder_2_out), .Q(S_PC_HIGH_q), .clk(not_9_out));  // open: en, clr
  not not_9 (not_9_out, PIN_CLK);
  ROM #(.dataWidth(10)) rom_2 (.addr(M_OPCODE_q), .data(rom_2_data));  // open: sel
  ROM #(.addrWidth(10)) rom_3 (
    .addr(M_UPC_q), .data({rom_3_data, s_pc_increment, s_PC_to_ADDR, s_write_mode}));  // open: sel
  ROM #(.addrWidth(10), .dataWidth(10)) rom_4 (.addr(S_UPC_q), .data(rom_4_data));  // open: sel
  ROM #(.addrWidth(10)) rom_5 (
    .addr(S_UPC_q),
    .data({rom_5_data[7:6], m_VEC_RESET_to_PC, m_load_uop_low, m_PC_to_PC, rom_5_data[2], m_reset_clear, m_load_opcode}));  // open: sel
  ROM #(.addrWidth(10)) rom_6 (
    .addr(S_UPC_q),
    .data({m_flag_set_emu, m_mux_in_flag_carry, m_flag_set_carry, m_mux_in_flag_mem, m_flag_set_mem}));  // open: sel
  ROM #(.addrWidth(10)) rom_7 (
    .addr(S_UPC_q), .data({rom_7_data, m_mux_in_flag_zero, m_flag_set_zero, m_mux_in_flag_emu}));  // open: sel
  RAM #(.addrWidth(16)) ram_1 (
    .addr(multiplexer_5_out), .data(ram_1_data), .clk(PIN_CLK), .ld(multiplexer_6_out));  // open: sel, clr
  not not_10 (not_10_out, multiplexer_6_out);
  assign ram_1_data = not_10_out ? multiplexer_7_out : 8'bz;  // Controlled_Buffer controlled_buffer_5
  assign BUS_ADDR_LOW = s_PC_to_ADDR ? S_PC_LOW_q : 8'bz;  // Controlled_Buffer controlled_buffer_6
  assign BUS_ADDR_HIGH = s_PC_to_ADDR ? S_PC_HIGH_q : 8'bz;  // Controlled_Buffer controlled_buffer_7
  Register #(.width(1), .trigger("high")) M_RESET (.D(S_RESET_q), .Q(re_reset_sig), .clk(PIN_CLK));  // open: en, clr
  assign PIN_DATA = multiplexer_6_out ? ram_1_data : 8'bz;  // Controlled_Buffer controlled_buffer_8
  not not_11 (not_11_out, S_FLAG_M);
  and and_5 (and_5_out, ~S_FLAG_E, S_FLAG_C);  // AND_Gate
  Multiplexer #(.select(2), .disabled(0), .enable("false")) multiplexer_8 (
    .in0(1'b0), .in1(in_1[1]), .in2(in_2), .out(multiplexer_8_out), .sel(m_mux_in_flag_zero));  // open: in3
  and and_6 (and_6_out, m_flag_set_zero, PIN_CLK);
  Register #(.width(1), .trigger("high")) M_FLAG_M (
    .D(multiplexer_9_out), .Q(M_FLAG_M_q), .clk(and_7_out));  // open: en, clr
  Multiplexer #(.select(2), .disabled(0), .enable("false")) multiplexer_9 (
    .in0(1'b1), .in1(S_FLAG_E), .in2(and_5_out), .in3(not_11_out), .out(multiplexer_9_out),
    .sel(m_mux_in_flag_mem));
  and and_7 (and_7_out, m_flag_set_mem, PIN_CLK);
  Register #(.width(1), .trigger("high")) M_FLAG_Z (
    .D(multiplexer_8_out), .Q(M_FLAG_Z_q), .clk(and_6_out));  // open: en, clr
  not not_12 (not_12_out, PIN_CLK);
  Register #(.width(1), .trigger("high")) u_S_FLAG_M (.D(M_FLAG_M_q), .Q(S_FLAG_M), .clk(not_13_out));  // open: en, clr
  not not_13 (not_13_out, PIN_CLK);
  Register #(.width(1), .trigger("high")) u_S_FLAG_Z (.D(M_FLAG_Z_q), .Q(S_FLAG_Z), .clk(not_12_out));  // open: en, clr

  // Other names for the same wires on the sheet: ALU_CARRY_OUT = in_2; BUS_DATA[7:0] = in_1

  // Notes on the sheet:
  //   contents of rom_1 (hex, n*v repeats v):
  //   18 fb a5 0 ef 0 c2 30 a9 0 3 ef 1 ef 2 64 2 a9 0 5 85 4 a5 2 8d 80 3 e2 20 a9 4 8d 82 3 cb cd 82 3
  //   f0 fa ad 82 3 f0 9 ef 82 e2 30 38 fb 4c 0 5 c2 20 a2 0 3 5c a0 40 0 42 92 4 e6 4 e6 4 88 d0 f6 a5 4
  //   f0 e0 e6 2 4c 16 4
  //   contents of rom_2 (hex, n*v repeats v):
  //   24*2 3 31*2 4 199*2
  //   contents of rom_3 (hex, n*v repeats v):
  //   6
  //   contents of rom_4 (hex, n*v repeats v):
  //   0 0 2
  //   contents of rom_5 (hex, n*v repeats v):
  //   19 22 0 4
endmodule
